# Fritzing sketch almabraxas-2-01.01 (saved by Fritzing 0.9.2b)
breadboards: 1

parts:
  GPS1 = Adafruit Ultimate GPS Breakout
  Teensy_3_1 = Teensy 3.1 with header
  microSD1 = MicroSD Breakout  # not connected
  C1 = Ceramic Capacitor [capacitance=100nF package="100 mil [THT, multilayer]"]
  Part1 = DeuLigne 1.1 - The Snootlab's LCD shield for Arduino  # not connected

nets:
  N1: GPS1.TX, Teensy_3_1.D0
  N2: GPS1.RX, Teensy_3_1.D1
  N3: GPS1.GND, C1.1
  N4: GPS1.VIN, C1.0

custom parts:
  Teensy 3.1 with header: The Teensy is a complete USB-based microcontoller development system, in a very small footprint, capable of implementing many types of projects. All programming is done via the USB port. No special programmer is needed, only a standard micro-USB cable and a PC or Macintosh with a USB port. It has a USB keyboard/mouse/joystick emulation stack and can be programmed through Arduino IDE.
  MicroSD Breakout: 5V-ready microSD Breakout with Level Shifter
