# Fritzing sketch almabraxas-2-01 (saved by Fritzing 0.9.2b)
circuit board: 20cm x 20cm
breadboards: 1

parts:
  GPS = Adafruit Ultimate GPS Breakout  # not connected
  microSD1 = MicroSD Breakout
  R78 = Recom R78 [package="TO220 [THT]"]  # not connected
  C3 = Electrolytic Capacitor [capacitance=1µF package="100 mil [THT, electrolytic]"]  # not connected
  D1 = Rectifier Diode [part_number=1N4001 package="300 mil [THT]"]  # not connected
  C5 = Capacitor [package=cap-pth-small2]  # not connected
  R79 = Resistor [tolerance=±5% resistance=220 package="2512 [SMD]"]  # not connected
  C6 = Capacitor [package=cap-pth-small2]
  C7 = Capacitor [package=cap-pth-small2]  # not connected

nets:
  N1: microSD1.GND, C6.1
  N2: microSD1.5V, C6.2

notes:
  VCC
  GND

custom parts:
  MicroSD Breakout: 5V-ready microSD Breakout with Level Shifter
  Recom R78: 5V DC switching Voltage Regulator
