# Fritzing sketch almabraxas-2-02 (saved by Fritzing 0.9.2b)
circuit board: 20cm x 20cm
breadboards: 1

parts:
  GPS = Adafruit Ultimate GPS Breakout  # not connected
  microSD1 = MicroSD Breakout
  C3 = Electrolytic Capacitor [capacitance=1µF package="100 mil [THT, electrolytic]"]  # not connected
  D1 = Rectifier Diode [part_number=1N4001 package="300 mil [THT]"]
  C5 = Capacitor [package=cap-pth-small2]  # not connected
  C6 = Capacitor [package=cap-pth-small2]
  C7 = Capacitor [package=cap-pth-small2]  # not connected
  VCC1 = Battery block 9V
  C8 = Capacitor Polarized [package=cpol-radial-100uf-25v]
  R78 = Recom R78 [package="TO220 [THT]"]
  R79 = Resistor [tolerance=±5% resistance=220 package=THT]  # not connected
  R80 = Resistor [tolerance=±5% resistance=220 package=THT]  # not connected

nets:
  N1: microSD1.GND, C6.1
  N2: microSD1.5V, C6.2
  N3: D1.cathode, VCC1.+, R78.+Vin
  N4: D1.anode, C8.+, R78.+Vout
  GND: VCC1.-, C8.-, R78.GND

notes:
  VCC
  GND
  Power block
  Battery voltage sensor

custom parts:
  MicroSD Breakout: 5V-ready microSD Breakout with Level Shifter
  Recom R78: 5V DC switching Voltage Regulator
