# Fritzing sketch almabraxas-2-03 (saved by Fritzing 0.9.2b)
circuit board: 20cm x 20cm
breadboards: 1

parts:
  GPS = Adafruit Ultimate GPS Breakout
  microSD1 = MicroSD Breakout
  D1 = Rectifier Diode [part_number=1N4001 package="300 mil [THT]"]
  C5 = Capacitor [package=cap-pth-small2]  # not connected
  C6 = Capacitor [package=cap-pth-small2]
  C7 = Capacitor [package=cap-pth-small2]  # not connected
  VCC1 = Battery block 9V
  C8 = Capacitor Polarized [package=cpol-radial-100uf-25v]
  R78 = Recom R785.0-1.0 [package="TO220 [THT]"]
  R79 = Resistor [tolerance=±5% resistance=2.2k package=THT]
  R80 = Resistor [tolerance=±5% resistance=4.7k package=THT]
  Teensy_3_1 = Teensy 3.1
  C9 = Capacitor [package=cap-pth-small2]

nets:
  GND: GPS.GND, VCC1.-, C8.-, R78.GND, R79.Pin_1, Teensy_3_1.GND, C9.2
  N1: microSD1.GND, C6.1
  N2: microSD1.5V, C6.2
  N3: D1.cathode, VCC1.+, R78.+Vin, R80.Pin_0
  N4: D1.anode, C8.+, R78.+Vout, Teensy_3_1.Vin, C9.1
  N5: R79.Pin_0, R80.Pin_1, Teensy_3_1.A2/D16

notes:
  VCC
  GND
  Power block
  Battery voltage sensor
  MCU

custom parts:
  MicroSD Breakout: 5V-ready microSD Breakout with Level Shifter
  Recom R785.0-1.0: 5V DC switching Voltage Regulator 1A (input voltage 6.5-18V)
