# Fritzing sketch almabraxas-2-05 (saved by Fritzing 0.9.2b)
circuit board: 20cm x 10cm
breadboards: 1

parts:
  GPS = Adafruit Ultimate GPS Breakout
  microSD1 = MicroSD Breakout
  D1 = Rectifier Diode [part_number=1N4001 package="300 mil [THT]"]
  C6 = Capacitor [package=cap-pth-small2]
  VCC1 = Battery block 9V
  C8 = Capacitor Polarized [package=cpol-radial-100uf-25v]
  R78 = Recom R785.0-1.0 [package="TO220 [THT]"]
  R79 = Resistor [tolerance=±5% resistance=2.2k package=THT]
  R80 = Resistor [tolerance=±5% resistance=4.7k package=THT]
  Teensy_3_1 = Teensy 3.1
  C9 = Capacitor [package=cap-pth-small2]
  Part1 = Barometric Pressure Sensor - BMP180 Breakout (GY-68)
  C10 = Capacitor [package=cap-pth-small2]
  Modem1 = Rockblock satellite modem connector [package=1x12_machine-pin-header_lock.004]  # not connected

nets:
  N1: GPS.TX, Teensy_3_1.D0
  N2: GPS.RX, Teensy_3_1.D1
  GND: GPS.GND, microSD1.GND, C6.1, VCC1.-, C8.-, R78.GND, R79.Pin_1, Teensy_3_1.GND, C9.2, Part1.GND, C10.2
  5V: microSD1.5V, D1.anode, C6.2, C8.+, R78.+Vout, Teensy_3_1.Vin, C9.1
  N3: D1.cathode, VCC1.+, R78.+Vin, R80.Pin_0
  N4: R79.Pin_0, R80.Pin_1
  3V3: Teensy_3_1.3V3, Part1.VCC, C10.1
  N5: Teensy_3_1.A4/D18, Part1.SDA
  N6: Teensy_3_1.A5/D19, Part1.SCL

notes:
  VCC
  GND
  Power block
  Battery voltage sensor
  MCU
  pressure + temp sensor

custom parts:
  MicroSD Breakout: 5V-ready microSD Breakout with Level Shifter
  Recom R785.0-1.0: 5V DC switching Voltage Regulator 1A (input voltage 6.5-18V)
  Rockblock satellite modem connector: Header 12 Standard 12-pin 0.1 header. Use with straight break away headers (SKU : PRT-00116), right angle break away headers (PRT-00553), swiss pins (PRT-00743), machine pins (PRT-00117), and female headers (PRT-00115).
