# Fritzing sketch almabraxas-2-10 (saved by Fritzing 0.9.3b)
circuit board: 20cm x 10cm
breadboards: 1

parts:
  GPS = Adafruit Ultimate GPS Breakout
  microSD1 = MicroSD Breakout
  D1 = Rectifier Diode [part_number=1N4001 package="300 mil [THT]"]
  C6 = Capacitor [package=cap-pth-small2]
  VCC1 = Battery block 9V
  C8 = Capacitor Polarized [package=cpol-radial-100uf-25v]
  R78 = Recom R785.0-1.0 [package="TO220 [THT]"]
  R79 = Resistor [tolerance=±5% resistance=2.2k package=THT]
  R80 = Resistor [tolerance=±5% resistance=4.7k package=THT]
  C9 = Capacitor [package=cap-pth-small2]
  C11 = Capacitor [package=cap-pth-small2]
  RB1 = RB1 connector [form="♀ (female)" package=THT]
  C12 = Capacitor [package=cap-pth-small2]
  Q1 = MOSFET-NCHANNEL [package=to-92]  # not connected
  Part1 = BMP180 Breakout (GY-68) + header
  Teensy_3_1 = Teensy 3.1
  LED1 = LED - 3mm [color="Red (633nm)" package="3 mm [THT]"]
  LED2 = LED - 3mm [color="Yellow (595nm)" package="3 mm [THT]"]  # not connected
  LED3 = LED - 3mm [color="Green (570nm)" package="3 mm [THT]"]
  LED4 = LED - 3mm [color="Yellow (595nm)" package="3 mm [THT]"]
  LED5 = LED - 3mm [color="Blue (525nm)" package="3 mm [THT]"]  # not connected
  R81 = Resistor [tolerance=±5% resistance=220 package=THT]  # not connected
  RA1 = Resistor array - 4 independant resistors [form="♀ (female)" package=THT]

nets:
  N1: GPS.TX, Teensy_3_1.D0
  N2: GPS.RX, Teensy_3_1.D1
  GND: GPS.GND, microSD1.GND, C6.1, VCC1.-, C8.-, R78.GND, R79.Pin_1, C9.2, C11.1, RB1.CTS, RB1.RTS, RB1.GND, C12.2, Part1.GND, LED1.cathode, LED3.cathode, LED4.cathode
  VIN: GPS.VIN, microSD1.5V, D1.anode, C6.2, C8.+, R78.+Vout, C9.1, C11.2, RB1.5V, Teensy_3_1.Vin
  N3: microSD1.CS, Teensy_3_1.A1/D15
  N4: microSD1.DI, Teensy_3_1.D11
  N5: microSD1.DO, Teensy_3_1.D12
  N6: microSD1.CLK, Teensy_3_1.A0/D14
  N7: VCC1.+, R78.+Vin, R80.Pin_0
  N8: R79.Pin_0, R80.Pin_1
  N9: RB1.TX, Teensy_3_1.D10
  N10: RB1.RX, Teensy_3_1.D9
  VCC: C12.1, Part1.VCC, Teensy_3_1.3V3
  N11: Part1.SCL, Teensy_3_1.A5/D19
  N12: Part1.SDA, Teensy_3_1.A4/D18
  N13: LED1.anode, RA1.pin5
  N14: LED3.anode, RA1.pin1
  N15: LED4.anode, RA1.pin3

notes:
  VCC
  GND
  Power block
  Battery voltage sensor
  MCU
  pressure + temp sensor
  SCL
  SDA

custom parts:
  MicroSD Breakout: 5V-ready microSD Breakout with Level Shifter
  Recom R785.0-1.0: 5V DC switching Voltage Regulator 1A (input voltage 6.5-18V)
  RB1 connector: Connector for RockBlock 1 satellite modem
  BMP180 Breakout (GY-68) + header: This is a simple breakout board for the BMP180, a high-precision, low-power barometric pressure sensor made by Bosch Sensortec. The range of measurement is from 300hPa to 1100hPa. The sensor can be supplied with voltage ranging from 1.8V to 3.6V. Operating temperature range is -40 to +85 °C. This particular breakout board (or perhaps the configuration) is produced by Shenzhen Keep Power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
  Resistor array - 4 independant resistors: 4 x resistors in an array
